# Fritzing sketch paste_dispenser (saved by Fritzing 0.9.3b)
circuit board: 5.8cm x 4.4cm
breadboards: 1

parts:
  PRO_MINI = Arduino Pro Mini v13
  Squix1 = OLED 0.91" 128x32 I2C SSD1306 (GND/VCC)
  PUSH = Pushbutton [package="[THT]"]
  FASTER = Pushbutton [package="[THT]"]
  SLOWER = Pushbutton [package="[THT]"]
  Part3 = FTDI Basic Programmer
  TB6612FNG = Adafruit TB6612 DC and Stepper Motor Driver [part_number="Adafruit #2448"]
  STEPPER = Adafruit Gear-Reduced Stepper Motor (small)
  PULL = Pushbutton [package="[THT]"]
  FOOTSWITCH = 2.5mm Audio Jack [package=stereojack2.5mm_stereojack2.5mm]

nets:
  N1: PRO_MINI.DTR, Part3.DTR
  N2: PRO_MINI.D0/TX, Part3.RXI
  N3: PRO_MINI.D1/RX, Part3.TXO
  VCC: PRO_MINI.VCC, Squix1.VCC, Part3.POWER, TB6612FNG.PWRIN, TB6612FNG.VCC
  GND: PRO_MINI.GND, Squix1.GND, PUSH.Pin_3, PUSH.Pin_4, FASTER.Pin_3, FASTER.Pin_4, SLOWER.Pin_3, SLOWER.Pin_4, Part3.CTS, Part3.GND, TB6612FNG.GND, STEPPER.RED, PULL.Pin_3, PULL.Pin_4, FOOTSWITCH.SLEEVE
  N4: PRO_MINI.A4, Squix1.SCA
  N5: PRO_MINI.A5, Squix1.SCL
  N6: PRO_MINI.A3, TB6612FNG.AIN1
  N7: PRO_MINI.A2, TB6612FNG.AIN2
  N8: PRO_MINI.A1, TB6612FNG.BIN1
  N9: PRO_MINI.A0, TB6612FNG.BIN2
  N10: PRO_MINI.D10_PWM/SS, TB6612FNG.PWMB
  N11: PRO_MINI.D9_PWM, TB6612FNG.PWMA
  N12: PRO_MINI.D8, TB6612FNG.STBY
  N13: PRO_MINI.D7, PULL.Pin_1, PULL.Pin_2
  N14: PRO_MINI.D6_PWM, PUSH.Pin_1, PUSH.Pin_2
  N15: PRO_MINI.D5_PWM, FASTER.Pin_1, FASTER.Pin_2
  N16: PRO_MINI.D4, SLOWER.Pin_1, SLOWER.Pin_2
  N17: PRO_MINI.D2, FOOTSWITCH.LEFT, FOOTSWITCH.RIGHT
  N18: TB6612FNG.MOTORA1, STEPPER.BLUE
  N19: TB6612FNG.MOTORA2, STEPPER.YELLOW
  N20: TB6612FNG.MOTORB2, STEPPER.PINK
  N21: TB6612FNG.MOTORB1, STEPPER.ORANGE

notes:
  Pushbuttons:
  Push Fast Slow Pull Footswitch
  Solder Paste Dispenser w/
  LED on pin 13.
  In sketch:
  pins.h:
  kLedPin = 13
  breathingled.cpp:
  #define LED_PWM 0

custom parts:
  OLED 0.91" 128x32 I2C SSD1306 (GND/VCC): OLED 0.91" 128x32 I2C SSD1306 Pinout: GND/VCC/SCL/SDA
  Adafruit TB6612 DC and Stepper Motor Driver: Spin two DC motors, step one bi-polar or uni-polar stepper, or fire off two solenoids with 1.2A per channel using the TB6612. These are perhaps better known as "the drivers in our assembled Adafruit Motorshield or Motor HAT." We really like these dual H-bridges, so if you want to control motors without a shield or HAT these are easy to include on any solderless breadboard or perma-proto.
  Adafruit Gear-Reduced Stepper Motor (small): Adafruit gear-reduction stepper motor (small)
